# Fritzing sketch bell (saved by Fritzing 0.9.4)

parts:
  Grove1 = Grove Button
  ESP32_-_Back1 = ESP32 - CAM
  USBUART1 = PL2303 USB UART Breakout
  Grove2 = Grove Buzz

nets:
  GND: Grove1.GND, ESP32_-_Back1.GND#7, Grove2.GND
  VCC: Grove1.VCC, ESP32_-_Back1.5V, USBUART1.VCCIO, Grove2.VCC
  N1: Grove1.NC, ESP32_-_Back1.GPIO14
  N2: Grove1.SIG, ESP32_-_Back1.GPIO15
  N3: ESP32_-_Back1.GPIO13, Grove2.SIG
  N4: ESP32_-_Back1.GND#12, USBUART1.GND
  N5: ESP32_-_Back1.GPIO3_/_RX, USBUART1.TXD
  N6: ESP32_-_Back1.GPIO1_/_TX, USBUART1.RXD

custom parts:
  ESP32 - CAM: The ESP32-CAM has a very competitive small-size camera module that can operate independently as a minimum system with a footprint of only 27*40.5*4.5mm and a deep sleep current of up to 6mA.
  PL2303 USB UART Breakout: PL2302 Usb Uart Breakout Board with Battery
